// Logisim project 7_Segments.circ as structural Verilog: 11 circuits, main circuit Binary_7_Segment_A
module Binary_7_Segment_A (
  input  A,
  input  B,
  input  C,
  input  D,
  output OA
);

  wire and_1_out, and_2_out, and_3_out, and_4_out, and_5_out, and_6_out, and_7_out, and_8_out, and_9_out,
       not_1_out, not_2_out, not_3_out, not_4_out, not_5_out, not_6_out, not_7_out, not_8_out, not_9_out,
       not_10_out, or_1_out, or_2_out;

  not not_1 (not_1_out, B);
  not not_2 (not_2_out, A);
  not not_3 (not_3_out, B);
  not not_4 (not_4_out, C);
  not not_5 (not_5_out, D);
  and and_1 (and_1_out, A, not_1_out);
  and and_2 (and_2_out, not_2_out, not_3_out);
  and and_3 (and_3_out, not_4_out, not_5_out);
  and and_4 (and_4_out, not_5_out, C);
  and and_5 (and_5_out, and_2_out, and_3_out);
  not not_6 (not_6_out, D);
  not not_7 (not_7_out, C);
  not not_8 (not_8_out, D);
  and and_6 (and_6_out, C, B, not_6_out);
  not not_9 (not_9_out, B);
  not not_10 (not_10_out, C);
  and and_7 (and_7_out, and_1_out, and_4_out);
  and and_8 (and_8_out, not_7_out, not_8_out, B);
  and and_9 (and_9_out, D, not_9_out, not_10_out);
  or or_1 (or_1_out, and_7_out, and_5_out);
  or or_2 (or_2_out, and_8_out, and_6_out, and_9_out);
  or or_3 (OA, or_1_out, or_2_out);
endmodule

module Binary_7_Segment_B (
  input  A,
  input  B,
  input  C,
  input  D,
  output Ob
);

  wire and_1_out, and_2_out, and_3_out, and_4_out, and_5_out, not_1_out, not_2_out, not_3_out, not_4_out,
       not_5_out, not_6_out, not_7_out, not_8_out, not_9_out, not_10_out, or_1_out, or_2_out, or_3_out;

  not not_1 (not_1_out, A);
  not not_2 (not_2_out, B);
  not not_3 (not_3_out, D);
  not not_4 (not_4_out, B);
  not not_5 (not_5_out, C);
  not not_6 (not_6_out, D);
  and and_1 (and_1_out, not_1_out, not_2_out, C, not_3_out);
  and and_2 (and_2_out, A, B, C, not_3_out);
  and and_3 (and_3_out, not_4_out, not_5_out, not_6_out);
  not not_7 (not_7_out, C);
  not not_8 (not_8_out, D);
  or or_1 (or_1_out, and_1_out, and_2_out);
  and and_4 (and_4_out, B, not_7_out, not_8_out);
  not not_9 (not_9_out, B);
  not not_10 (not_10_out, C);
  and and_5 (and_5_out, not_9_out, not_10_out, D);
  or or_2 (or_2_out, or_1_out, and_3_out);
  or or_3 (or_3_out, or_2_out, and_4_out);
  or or_4 (Ob, or_3_out, and_5_out);
endmodule

module Binary_7_Segment_C (
  input  A,
  input  B,
  input  C,
  input  D,
  output Oc
);

  wire and_1_out, and_2_out, and_3_out, and_4_out, and_5_out, not_1_out, not_2_out, not_3_out, not_4_out,
       not_5_out, not_6_out, not_7_out, not_8_out, not_9_out, not_10_out, or_1_out, or_2_out, or_3_out;

  not not_1 (not_1_out, C);
  not not_2 (not_2_out, D);
  and and_1 (and_1_out, A, B, not_1_out, not_2_out);
  not not_3 (not_3_out, B);
  not not_4 (not_4_out, C);
  and and_2 (and_2_out, not_3_out, not_4_out, not_5_out);
  not not_5 (not_5_out, D);
  not not_6 (not_6_out, B);
  not not_7 (not_7_out, D);
  not not_8 (not_8_out, D);
  and and_3 (and_3_out, not_6_out, C, not_7_out);
  and and_4 (and_4_out, B, C, not_8_out);
  not not_9 (not_9_out, B);
  not not_10 (not_10_out, C);
  or or_1 (or_1_out, and_1_out, and_2_out);
  and and_5 (and_5_out, not_9_out, not_10_out, D);
  or or_2 (or_2_out, or_1_out, and_3_out);
  or or_3 (or_3_out, and_4_out, and_5_out);
  or or_4 (Oc, or_2_out, or_3_out);
endmodule

module Binary_7_Segment_D (
  input  A,
  input  B,
  input  C,
  input  D,
  output Od
);

  wire and_1_out, and_2_out, and_3_out, and_4_out, and_5_out, not_1_out, not_2_out, not_3_out, not_4_out,
       not_5_out, not_6_out, not_7_out, not_8_out, not_9_out, not_10_out, not_11_out, not_12_out, or_1_out;

  not not_1 (not_1_out, A);
  not not_2 (not_2_out, B);
  not not_3 (not_3_out, C);
  not not_4 (not_4_out, D);
  not not_5 (not_5_out, B);
  not not_6 (not_6_out, D);
  not not_7 (not_7_out, A);
  not not_8 (not_8_out, D);
  not not_9 (not_9_out, C);
  not not_10 (not_10_out, D);
  not not_11 (not_11_out, B);
  not not_12 (not_12_out, C);
  and and_1 (and_1_out, A, not_5_out, C, not_6_out);
  and and_2 (and_2_out, not_7_out, B, C, not_8_out);
  and and_3 (and_3_out, B, not_9_out, not_10_out);
  and and_4 (and_4_out, not_11_out, not_12_out, D);
  and and_5 (and_5_out, not_1_out, not_2_out, not_3_out, not_4_out);
  or or_1 (or_1_out, and_1_out, and_2_out, and_3_out, and_4_out);
  or or_2 (Od, and_5_out, or_1_out);
endmodule

module Binary_7_Segment_E (
  input  A,
  input  B,
  input  C,
  input  D,
  output Oe
);

  wire and_1_out, and_2_out, and_3_out, and_4_out, not_1_out, not_2_out, not_3_out, not_4_out, not_5_out,
       not_6_out, not_7_out, not_8_out, not_9_out, not_10_out, not_11_out, not_12_out, or_1_out, or_2_out;

  not not_1 (not_1_out, A);
  not not_2 (not_2_out, B);
  not not_3 (not_3_out, C);
  not not_4 (not_4_out, D);
  not not_5 (not_5_out, A);
  not not_6 (not_6_out, C);
  not not_7 (not_7_out, D);
  and and_1 (and_1_out, not_5_out, B, not_6_out, not_7_out);
  and and_2 (and_2_out, not_1_out, not_2_out, not_3_out, not_4_out);
  not not_8 (not_8_out, A);
  not not_9 (not_9_out, D);
  not not_10 (not_10_out, A);
  not not_11 (not_11_out, B);
  not not_12 (not_12_out, C);
  or or_1 (or_1_out, and_2_out, and_1_out);
  and and_3 (and_3_out, not_8_out, B, C, not_9_out);
  and and_4 (and_4_out, not_10_out, not_11_out, not_12_out, D);
  or or_2 (or_2_out, and_3_out, and_4_out);
  or or_3 (Oe, or_1_out, or_2_out);
endmodule

module Binary_7_Segment_F (
  input  in_1,
  input  in_2,
  input  in_3,
  input  in_4,
  output O_F
);

  wire and_1_out, and_2_out, and_3_out, and_4_out, not_1_out, not_2_out, not_3_out, not_4_out, not_5_out,
       not_6_out, not_7_out, not_8_out, not_9_out, not_10_out, or_1_out, or_2_out;

  not not_1 (not_1_out, in_1);
  not not_2 (not_2_out, in_2);
  not not_3 (not_3_out, in_3);
  not not_4 (not_4_out, in_4);
  not not_5 (not_5_out, in_1);
  not not_6 (not_6_out, in_4);
  and and_1 (and_1_out, not_5_out, in_2, in_3, not_6_out);
  not not_7 (not_7_out, in_2);
  not not_8 (not_8_out, in_4);
  not not_9 (not_9_out, in_2);
  not not_10 (not_10_out, in_3);
  and and_2 (and_2_out, not_7_out, in_3, not_8_out);
  and and_3 (and_3_out, not_9_out, not_10_out, in_4);
  and and_4 (and_4_out, not_1_out, not_2_out, not_3_out, not_4_out);
  or or_1 (or_1_out, and_2_out, and_3_out);
  or or_2 (or_2_out, and_4_out, and_1_out);
  or or_3 (O_F, or_2_out, or_1_out);
endmodule

module Binary_7_Segments_G (
  input  A,
  input  B,
  input  C,
  input  D,
  output og
);

  wire and_1_out, and_2_out, and_3_out, and_4_out, not_1_out, not_2_out, not_3_out, not_4_out, not_5_out,
       not_6_out, not_7_out, not_8_out, or_1_out, or_2_out;

  not not_1 (not_1_out, A);
  not not_2 (not_2_out, D);
  not not_3 (not_3_out, C);
  not not_4 (not_4_out, D);
  not not_5 (not_5_out, B);
  not not_6 (not_6_out, D);
  and and_1 (and_1_out, B, not_3_out, not_4_out);
  and and_2 (and_2_out, not_5_out, C, not_6_out);
  not not_7 (not_7_out, B);
  not not_8 (not_8_out, C);
  and and_3 (and_3_out, not_1_out, B, C, not_2_out);
  and and_4 (and_4_out, not_7_out, not_8_out, D);
  or or_1 (or_1_out, and_3_out, and_1_out);
  or or_2 (or_2_out, and_2_out, and_4_out);
  or or_3 (og, or_1_out, or_2_out);
endmodule

module Binary_7_Segment (
  input  D,
  input  C,
  input  B,
  input  A,
  output OA,
  output OB,
  output OC,
  output OD,
  output OE,
  output O_F,
  output OG
);

  Binary_7_Segment_A binary_7_segment_a_1 (.A(A), .B(B), .C(C), .D(D), .OA(OA));
  Binary_7_Segment_B binary_7_segment_b_1 (.A(A), .B(B), .C(C), .D(D), .Ob(OB));
  Binary_7_Segment_C binary_7_segment_c_1 (.A(A), .B(B), .C(C), .D(D), .Oc(OC));
  Binary_7_Segment_D binary_7_segment_d_1 (.A(A), .B(B), .C(C), .D(D), .Od(OD));
  Binary_7_Segment_E binary_7_segment_e_1 (.A(A), .B(B), .C(C), .D(D), .Oe(OE));
  Binary_7_Segment_F binary_7_segment_f_1 (.in_1(A), .in_2(B), .in_3(C), .in_4(D), .O_F(O_F));
  Binary_7_Segments_G binary_7_segments_g_1 (.A(A), .B(B), .C(C), .D(D), .og(OG));
endmodule

module main (
  input  in_1,
  input  in_2
);

  wire binary_7_segment_1_o_f, binary_7_segment_1_oa, binary_7_segment_1_ob, binary_7_segment_1_oc,
       binary_7_segment_1_od, binary_7_segment_1_oe, binary_7_segment_1_og, clock_1_out;
  wire [3:0] counter_1_q;

  Clock clock_1 (.out(clock_1_out));
  Counter #(.max('h9), .width(4)) counter_1 (
    .count(in_1), .Q(counter_1_q), .clk(clock_1_out), .clr(in_2));  // open: load, D, carry, up
  Binary_7_Segment binary_7_segment_1 (
    .D(counter_1_q[3]), .C(counter_1_q[2]), .B(counter_1_q[1]), .A(counter_1_q[0]),
    .OA(binary_7_segment_1_oa), .OB(binary_7_segment_1_ob), .OC(binary_7_segment_1_oc),
    .OD(binary_7_segment_1_od), .OE(binary_7_segment_1_oe), .O_F(binary_7_segment_1_o_f),
    .OG(binary_7_segment_1_og));
  _7_Segment_Display u_7_segment_display_1 (
    .g(binary_7_segment_1_og), .f(binary_7_segment_1_o_f), .a(binary_7_segment_1_oa),
    .b(binary_7_segment_1_ob), .e(binary_7_segment_1_oe), .d(binary_7_segment_1_od), .c(binary_7_segment_1_oc));  // open: dp
endmodule

module Binary_0_to_99_Segement (
  input  CLK,
  input  Reset,
  output out_3,
  output out_4,
  output out_5,
  output out_6
);

  wire A_qn, and_1_out, B_qn, C_qn, or_1_out;

  J_K_Flip_Flop D (.J(1'b1), .clk(C_qn), .K(1'b1), .Q(out_3), .reset(or_1_out));  // open: Qn, preset
  J_K_Flip_Flop C (.J(1'b1), .clk(B_qn), .K(1'b1), .Q(out_4), .Qn(C_qn), .reset(or_1_out));  // open: preset
  J_K_Flip_Flop B (.J(1'b1), .clk(A_qn), .K(1'b1), .Q(out_5), .Qn(B_qn), .reset(or_1_out));  // open: preset
  J_K_Flip_Flop A (.J(1'b1), .clk(CLK), .K(1'b1), .Q(out_6), .Qn(A_qn), .reset(or_1_out));  // open: preset
  or or_1 (or_1_out, and_1_out, Reset);
  and and_1 (and_1_out, out_3, out_5);
endmodule

module main_binary_99 (
  input  in_1
);

  wire binary_0_to_99_segement_1_out_3, binary_0_to_99_segement_1_out_4, binary_0_to_99_segement_1_out_5,
       binary_0_to_99_segement_1_out_6, binary_0_to_99_segement_2_out_3, binary_0_to_99_segement_2_out_4,
       binary_0_to_99_segement_2_out_5, binary_0_to_99_segement_2_out_6, binary_7_segment_1_o_f,
       binary_7_segment_1_oa, binary_7_segment_1_ob, binary_7_segment_1_oc, binary_7_segment_1_od,
       binary_7_segment_1_oe, binary_7_segment_1_og, binary_7_segment_2_o_f, binary_7_segment_2_oa,
       binary_7_segment_2_ob, binary_7_segment_2_oc, binary_7_segment_2_od, binary_7_segment_2_oe,
       binary_7_segment_2_og, clock_1_out, not_1_out;

  Binary_7_Segment binary_7_segment_1 (
    .D(binary_0_to_99_segement_1_out_3), .C(binary_0_to_99_segement_1_out_4),
    .B(binary_0_to_99_segement_1_out_5), .A(binary_0_to_99_segement_1_out_6), .OA(binary_7_segment_1_oa),
    .OB(binary_7_segment_1_ob), .OC(binary_7_segment_1_oc), .OD(binary_7_segment_1_od),
    .OE(binary_7_segment_1_oe), .O_F(binary_7_segment_1_o_f), .OG(binary_7_segment_1_og));
  Binary_0_to_99_Segement binary_0_to_99_segement_1 (
    .CLK(not_1_out), .Reset(in_1), .out_3(binary_0_to_99_segement_1_out_3),
    .out_4(binary_0_to_99_segement_1_out_4), .out_5(binary_0_to_99_segement_1_out_5),
    .out_6(binary_0_to_99_segement_1_out_6));
  _7_Segment_Display u_7_segment_display_1 (
    .g(binary_7_segment_1_og), .f(binary_7_segment_1_o_f), .a(binary_7_segment_1_oa),
    .b(binary_7_segment_1_ob), .e(binary_7_segment_1_oe), .d(binary_7_segment_1_od), .c(binary_7_segment_1_oc));  // open: dp
  not not_1 (not_1_out, binary_0_to_99_segement_2_out_3);
  Binary_7_Segment binary_7_segment_2 (
    .D(binary_0_to_99_segement_2_out_3), .C(binary_0_to_99_segement_2_out_4),
    .B(binary_0_to_99_segement_2_out_5), .A(binary_0_to_99_segement_2_out_6), .OA(binary_7_segment_2_oa),
    .OB(binary_7_segment_2_ob), .OC(binary_7_segment_2_oc), .OD(binary_7_segment_2_od),
    .OE(binary_7_segment_2_oe), .O_F(binary_7_segment_2_o_f), .OG(binary_7_segment_2_og));
  Binary_0_to_99_Segement binary_0_to_99_segement_2 (
    .CLK(clock_1_out), .Reset(in_1), .out_3(binary_0_to_99_segement_2_out_3),
    .out_4(binary_0_to_99_segement_2_out_4), .out_5(binary_0_to_99_segement_2_out_5),
    .out_6(binary_0_to_99_segement_2_out_6));
  Clock clock_1 (.out(clock_1_out));
  _7_Segment_Display u_7_segment_display_2 (
    .g(binary_7_segment_2_og), .f(binary_7_segment_2_o_f), .a(binary_7_segment_2_oa),
    .b(binary_7_segment_2_ob), .e(binary_7_segment_2_oe), .d(binary_7_segment_2_od), .c(binary_7_segment_2_oc));  // open: dp
endmodule
